// Logisim project corg2part2.circ as structural Verilog: 1 circuit, main circuit main
module main (
  input  [3:0] RegSel,
  input  [1:0] OutBSel,
  input  MuxCSel,
  input  [3:0] FunSel,
  input  [1:0] FunSel_2,
  input  [1:0] OutASel,
  input  Enable,
  input  Reset,
  input  [1:0] MuxASel,
  input  [2:0] RegSel_2,
  input  [1:0] FunSel_3,
  input  [1:0] OutCSel,
  input  [1:0] MuxBSel,
  input  in_14,
  input  in_15,
  input  [1:0] OutCSel_2,
  input  in_17,
  input  in_18,
  input  L_H_prime,
  input  Enable_2,
  input  [1:0] FunSel_4,
  output [3:0] Z_C_N_O
);

  wire main_1_p4, main_4_p6, not_1_out;
  wire [3:0] main_1_p7, main_1_p7_2, main_1_p8, main_1_p8_2, main_2_p6, main_2_p6_2, main_2_p7, main_2_p7_2;
  wire [7:0] main_2_p5, main_2_p6_3, main_2_p8, main_4_p5, multiplexer_1_out, multiplexer_2_out,
       multiplexer_3_out;

  Hex_Digit_Display hex_digit_display_1 (.value(main_1_p7_2));  // open: dp
  Hex_Digit_Display hex_digit_display_2 (.value(multiplexer_1_out[7:4]));  // open: dp
  Hex_Digit_Display hex_digit_display_3 (.value(main_1_p8_2));  // open: dp
  Hex_Digit_Display hex_digit_display_4 (.value(main_1_p7));  // open: dp
  Hex_Digit_Display hex_digit_display_5 (.value(multiplexer_1_out[3:0]));  // open: dp
  Hex_Digit_Display hex_digit_display_6 (.value(main_2_p6_2));  // open: dp
  Hex_Digit_Display hex_digit_display_7 (.value(main_1_p8));  // open: dp
  Multiplexer #(.select(2), .width(8), .enable("false")) multiplexer_1 (
    .in0({main_2_p6_2, main_2_p6}), .in1(main_2_p5), .in2(main_2_p8), .in3(main_4_p5),
    .out(multiplexer_1_out), .sel(MuxASel));
  Hex_Digit_Display hex_digit_display_8 (.value(main_2_p6));  // open: dp
  // part2a_main main_1: pin names not known; wires that end beside it: multiplexer_1_out, RegSel, FunSel_2, main_1_p4, OutASel, OutBSel, {main_1_p7_2, main_1_p7}, {main_1_p8_2, main_1_p8}
  not not_1 (not_1_out, L_H_prime);
  Multiplexer #(.width(8), .enable("false")) multiplexer_2 (
    .in0(multiplexer_1_out), .in1({main_1_p7_2, main_1_p7}), .out(multiplexer_2_out), .sel(MuxCSel));
  // Part2c_main main_2: pin names not known; wires that end beside it: not_1_out, main_1_p4, Enable_2, FunSel_4, main_2_p5, {main_2_p6_3, main_2_p6_2, main_2_p6}, {main_2_p7_2, main_2_p7}, main_2_p8
  Hex_Digit_Display hex_digit_display_9 (.value(main_2_p7_2));  // open: dp
  Multiplexer #(.select(2), .width(8), .enable("false")) multiplexer_3 (
    .in0(multiplexer_3_out), .in1({main_2_p6_2, main_2_p6}), .in2(main_2_p5), .in3(main_4_p5),
    .out(multiplexer_3_out), .sel(MuxBSel));
  Hex_Digit_Display hex_digit_display_10 (.value(main_2_p7));  // open: dp
  // part2b_main main_3: pin names not known; wires that end beside it: multiplexer_3_out, RegSel_2, FunSel_3, main_1_p4, OutCSel_2, OutCSel, main_2_p8, {main_2_p7_2, main_2_p7}
  Hex_Digit_Display hex_digit_display_11 (.value(main_2_p8[3:0]));  // open: dp
  Hex_Digit_Display hex_digit_display_12 (.value(main_2_p8[7:4]));  // open: dp
  Hex_Digit_Display hex_digit_display_13 (.value(main_4_p5[7:4]));  // open: dp
  // corg_P2_main main_4: pin names not known; wires that end beside it: multiplexer_2_out, {main_1_p8_2, main_1_p8}, Z_C_N_O[2], FunSel, main_4_p5, main_4_p6
  Hex_Digit_Display hex_digit_display_14 (.value(main_4_p5[3:0]));  // open: dp
  // _4_bit_load_only_reg_main main_5: pin names not known; wires that end beside it: main_1_p4, Enable, main_4_p6, Z_C_N_O, Reset
  Hex_Digit_Display hex_digit_display_15 (.value(main_2_p5[3:0]));  // open: dp
  Hex_Digit_Display hex_digit_display_16 (.value(main_2_p5[7:4]));  // open: dp
  Clock clock_1 (.out(main_1_p4));
  RAM #(.bus("separate")) ram_1 (
    .addr({main_2_p7_2, main_2_p7}), .din(main_4_p5), .data(main_2_p5), .str(in_14), .sel(in_17),
    .clk(main_1_p4), .ld(in_18), .clr(in_15));

  // Notes on the sheet:
  //   OutA
  //   MuxAOut
  //   IROut (0-7)
  //   OutB
  //   Adress Reg OutD
  //   Adress Reg OutC
  //   OutALU
  //   Memory Output
endmodule
